# Fritzing sketch SensorStation (saved by Fritzing 0.9.2b)
circuit board: 9.94948cm x 7.22058cm
breadboards: 1

parts:
  J1 = shrouded pin header, 8 pins [form="♂ (shrouded male)"]
  U1 = Voltage Regulator - 3.3V [package="TO220 [THT]"]
  R2 = Resistor [tolerance=±5% resistance=10k package=THT]
  R3 = Resistor [tolerance=±5% resistance=10k package=THT]
  R4 = Resistor [tolerance=±5% resistance=10k package=THT]
  I2C = Header 4 [package=screwterminal-3.5mm-4_lock]
  R1 = Resistor [tolerance=±5% resistance=4.7k package=THT]
  U2 = LIPO-1000mAh [package=lipo-1000]
  C1 = Electrolytic Capacitor [capacitance=1000µF voltage=50V package="300 mil [THT, electrolytic]"]
  RESET = Momentary Switch [package=ksa_sealed_tac_switch]
  DS18B20 = Header 3 [package=1x03-1mm-ra]
  R5 = Resistor [tolerance=±5% resistance=10k package=THT]

nets (from the schematic view):
  N1: J1.pin1, U1.GND, I2C.2, U2.-, C1.-, RESET.1, DS18B20.2
  N2: J1.pin2, R1.Pin_1, DS18B20.3
  N3: J1.pin3, R2.Pin_1, I2C.3
  N4: J1.pin4, R3.Pin_1
  N5: J1.pin5, I2C.4, R5.Pin_1
  N6: J1.pin6, R4.Pin_1, RESET.3
  N7: J1.pin8, U1.output_voltage, R2.Pin_0, R3.Pin_0, R4.Pin_0, I2C.1, R1.Pin_0, C1.+, DS18B20.1, R5.Pin_0
  N8: U1.input_voltage, U2.+

notes:
  ESP8266
